// Logisim project ALU.circ as structural Verilog: 1 circuit, main circuit main
module main (
  input  a0,
  input  a1,
  input  in_3,
  input  in_4,
  input  in_5,
  input  b0,
  input  b1,
  input  cin,
  output s0,
  output s1,
  output cout
);

  wire and_1_out, and_2_out, and_3_out, and_4_out, and_5_out, and_6_out, and_7_out, and_8_out, and_9_out,
       and_10_out, and_11_out, and_12_out, and_13_out, and_14_out, and_15_out, and_16_out, and_17_out,
       and_18_out, and_19_out, and_20_out, and_21_out, and_22_out, and_23_out, and_24_out, and_25_out,
       and_26_out, and_27_out, and_28_out, and_29_out, and_30_out, and_31_out, and_32_out, and_33_out,
       and_34_out, and_35_out, and_36_out, and_37_out, and_38_out, and_39_out, and_40_out, and_41_out,
       and_42_out, and_43_out, and_44_out, and_45_out, not_1_out, not_2_out, not_3_out, not_4_out, not_5_out,
       not_6_out, not_7_out, not_8_out, not_9_out, not_10_out, not_11_out, not_12_out, not_13_out,
       not_14_out, not_15_out, not_16_out, not_17_out, not_18_out, not_19_out, or_1_out, or_2_out, or_3_out,
       or_4_out, or_5_out, or_6_out, or_7_out, or_8_out, or_10_out, or_12_out, xor_1_out, xor_2_out,
       xor_3_out, xor_4_out, xor_5_out, xor_6_out, xor_7_out, xor_8_out, xor_9_out, xor_10_out, xor_11_out,
       xor_12_out, xor_13_out, xor_14_out, xor_15_out, xor_16_out, xor_17_out, xor_18_out, xor_19_out,
       xor_20_out, xor_21_out, xor_22_out, xor_23_out, xor_24_out, xor_25_out, xor_26_out;

  xor xor_1 (xor_1_out, a0, b0);
  xor xor_2 (xor_2_out, a1, b1);
  and and_1 (and_1_out, a0, b0);
  and and_2 (and_2_out, a1, b1);
  xor xor_3 (xor_3_out, a0, b0);
  xor xor_4 (xor_4_out, xor_3_out, 1'b0);
  xor xor_5 (xor_5_out, a0, b0);
  xor xor_6 (xor_6_out, xor_5_out, cin);
  xor xor_7 (xor_7_out, a0, b0);
  xor xor_8 (xor_8_out, xor_7_out, 1'b0);
  not not_1 (not_1_out, b0);
  not not_2 (not_2_out, xor_7_out);
  xor xor_9 (xor_9_out, a0, b0);
  xor xor_10 (xor_10_out, xor_9_out, cin);
  not not_3 (not_3_out, b0);
  not not_4 (not_4_out, xor_9_out);
  xor xor_11 (xor_11_out, b0, a0);
  xor xor_12 (xor_12_out, xor_11_out, 1'b0);
  not not_5 (not_5_out, a0);
  not not_6 (not_6_out, xor_11_out);
  xor xor_13 (xor_13_out, b0, a0);
  xor xor_14 (xor_14_out, xor_13_out, cin);
  not not_7 (not_7_out, a0);
  not not_8 (not_8_out, xor_13_out);
  and and_3 (and_3_out, a0, b0);
  or or_1 (or_1_out, and_3_out, and_4_out);
  and and_4 (and_4_out, xor_3_out, 1'b0);
  and and_5 (and_5_out, a0, b0);
  or or_2 (or_2_out, and_5_out, and_6_out);
  and and_6 (and_6_out, xor_5_out, cin);
  and and_7 (and_7_out, a0, not_1_out);
  or or_3 (or_3_out, and_7_out, and_8_out);
  and and_8 (and_8_out, not_2_out, 1'b0);
  and and_9 (and_9_out, a0, not_3_out);
  or or_4 (or_4_out, and_9_out, and_10_out);
  and and_10 (and_10_out, not_4_out, cin);
  and and_11 (and_11_out, b0, not_5_out);
  or or_5 (or_5_out, and_11_out, and_12_out);
  and and_12 (and_12_out, not_6_out, 1'b0);
  and and_13 (and_13_out, b0, not_7_out);
  or or_6 (or_6_out, and_13_out, and_14_out);
  and and_14 (and_14_out, not_8_out, cin);
  xor xor_15 (xor_15_out, a1, b1);
  xor xor_16 (xor_16_out, a1, b1);
  xor xor_17 (xor_17_out, a1, b1);
  not not_9 (not_9_out, b1);
  xor xor_18 (xor_18_out, a1, b1);
  not not_10 (not_10_out, b1);
  xor xor_19 (xor_19_out, b1, a1);
  not not_11 (not_11_out, a1);
  xor xor_20 (xor_20_out, b1, a1);
  not not_12 (not_12_out, a1);
  xor xor_21 (xor_21_out, xor_15_out, or_1_out);
  and and_15 (and_15_out, a1, b1);
  and and_16 (and_16_out, xor_15_out, or_1_out);
  xor xor_22 (xor_22_out, xor_16_out, or_2_out);
  and and_17 (and_17_out, a1, b1);
  and and_18 (and_18_out, xor_16_out, or_2_out);
  xor xor_23 (xor_23_out, xor_17_out, or_3_out);
  and and_19 (and_19_out, a1, not_9_out);
  not not_13 (not_13_out, xor_17_out);
  and and_20 (and_20_out, not_13_out, or_3_out);
  xor xor_24 (xor_24_out, xor_18_out, or_4_out);
  and and_21 (and_21_out, a1, not_10_out);
  not not_14 (not_14_out, xor_18_out);
  and and_22 (and_22_out, not_14_out, or_4_out);
  xor xor_25 (xor_25_out, xor_19_out, or_5_out);
  and and_23 (and_23_out, b1, not_11_out);
  not not_15 (not_15_out, xor_19_out);
  and and_24 (and_24_out, not_15_out, or_5_out);
  xor xor_26 (xor_26_out, xor_20_out, or_6_out);
  and and_25 (and_25_out, b1, not_12_out);
  not not_16 (not_16_out, xor_20_out);
  and and_26 (and_26_out, not_16_out, or_6_out);
  or or_7 (or_7_out, and_15_out, and_16_out);
  or or_8 (or_8_out, and_17_out, and_18_out);
  // OR_Gate or_9 has open pins: in0=and_19_out, in1=and_20_out, out=open
  or or_10 (or_10_out, and_21_out, and_22_out);
  // OR_Gate or_11 has open pins: in0=and_23_out, in1=and_24_out, out=open
  or or_12 (or_12_out, and_25_out, and_26_out);
  not not_17 (not_17_out, in_5);
  not not_18 (not_18_out, in_4);
  not not_19 (not_19_out, in_3);
  and and_27 (and_27_out, not_17_out, not_18_out, not_19_out, xor_1_out);
  and and_28 (and_28_out, in_5, not_18_out, not_19_out, and_1_out);
  and and_29 (and_29_out, not_17_out, in_4, not_19_out, xor_4_out);
  and and_30 (and_30_out, in_5, in_4, not_19_out, xor_6_out);
  and and_31 (and_31_out, not_17_out, not_18_out, in_3, xor_12_out);
  and and_32 (and_32_out, in_5, not_18_out, in_3, xor_14_out);
  and and_33 (and_33_out, not_17_out, in_4, in_3, xor_8_out);
  and and_34 (and_34_out, in_5, in_4, in_3, xor_10_out);
  and and_35 (and_35_out, not_17_out, not_18_out, not_19_out, xor_2_out);
  and and_36 (and_36_out, in_5, not_18_out, not_19_out, and_2_out);
  and and_37 (and_37_out, not_17_out, in_4, not_19_out, xor_21_out);
  and and_38 (and_38_out, in_5, in_4, not_19_out, xor_22_out);
  and and_39 (and_39_out, not_17_out, not_18_out, in_3, xor_25_out);
  and and_40 (and_40_out, in_5, not_18_out, in_3, xor_26_out);
  and and_41 (and_41_out, not_17_out, in_4, in_3, xor_23_out);
  and and_42 (and_42_out, in_5, in_4, in_3, xor_24_out);
  and and_43 (and_43_out, in_5, in_4, not_19_out, or_8_out);
  and and_44 (and_44_out, in_5, not_18_out, in_3, or_12_out);
  and and_45 (and_45_out, in_5, in_4, in_3, or_10_out);
  or or_13 (s0, and_27_out, and_28_out, and_29_out, and_30_out, and_31_out, and_32_out, and_33_out, and_34_out);
  or or_14 (s1, and_35_out, and_36_out, and_37_out, and_38_out, and_39_out, and_40_out, and_41_out, and_42_out);
  or or_15 (cout, and_43_out, and_44_out, and_45_out);
endmodule
